# Fritzing sketch Lab5_Sketch (saved by Fritzing 0.9.9b)
breadboards: 1

parts:
  Part1 = Arduino Uno (Rev3)
  R3 = Trimmer Potentiometer [maximum_resistance=10kΩ package=THT]
  R4 = Resistor [tolerance=±5% resistance=220 package="0603 [SMD]"]
  R5 = Resistor [tolerance=±5% resistance=220 package="0603 [SMD]"]
  R6 = Resistor [tolerance=±5% resistance=220 package="0603 [SMD]"]
  R7 = Resistor [tolerance=±5% resistance=220 package="0603 [SMD]"]
  R8 = Resistor [tolerance=±5% resistance=220 package="0603 [SMD]"]
  LED1 = smd LED [color="Red (633nm)" package="0805 [SMD]"]
  LED2 = smd LED [color="Blue (470nm)" package="0805 [SMD]"]
  LED3 = smd LED [color="Blue (470nm)" package="0805 [SMD]"]
  LED4 = smd LED [color="Red (633nm)" package="0805 [SMD]"]
  LED5 = smd LED [color="Red (633nm)" package="0805 [SMD]"]

nets:
  N1: Part1.A0, R3.wiper
  N2: Part1.D8, R4.Pin_1
  N3: Part1.D4, R6.Pin_1
  N4: Part1.D5_PWM, R7.Pin_1
  N5: Part1.D6_PWM, R8.Pin_1
  N6: Part1.D7, R5.Pin_1
  N7: Part1.5V, R3.leg2
  N8: Part1.GND, R3.leg1, LED2.cathode, LED4.cathode, LED5.cathode
  N9: R4.Pin_0, LED1.anode
  N10: R5.Pin_0, LED2.anode
  N11: R6.Pin_0, LED4.anode
  N12: R7.Pin_0, LED3.anode
  N13: R8.Pin_0, LED5.anode
